# Fritzing sketch Anzeige1 (saved by Fritzing 0.9.2b)
circuit board: 8.46667cm x 5.64444cm
breadboards: 1

parts:
  Arduino_Nano = Arduino Nano (Rev3.0)
  U1_LCD = LCD-16X2 [package=lcd-16x2]
  R2 = Resistor [tolerance=±5% resistance=220 package=THT]
  S1 = Round Pushbutton
  S2 = Round Pushbutton
  S3 = Round Pushbutton
  R1 = TRIMPOT [part_number=10ko package=trimpot-5mm]

nets:
  GND: Arduino_Nano.GND, U1_LCD.VSS, U1_LCD.R_W, U1_LCD.K, S1.leg1, S2.leg1, S3.leg0, R1.CCW
  N1: Arduino_Nano.D2, U1_LCD.DB7
  N2: Arduino_Nano.D3, U1_LCD.DB6
  N3: Arduino_Nano.D4, U1_LCD.DB5
  N4: Arduino_Nano.D5, U1_LCD.DB4
  N5: Arduino_Nano.D6, S1.leg0
  N6: Arduino_Nano.D7, S2.leg0
  N7: Arduino_Nano.D8, S3.leg1
  N8: Arduino_Nano.D9, U1_LCD.E
  N9: Arduino_Nano.D10, U1_LCD.RS
  5V: Arduino_Nano.5V, U1_LCD.VDD, R2.Pin_0, R1.CW
  N10: U1_LCD.VO, R1.WIPER
  N11: U1_LCD.A, R2.Pin_1
