# Fritzing sketch rus_1 (saved by Fritzing 0.9.2b)
circuit board: 8.46667cm x 5.64444cm
breadboards: 1

parts:
  U1 = NodeMCU V1.0
  DHT1 = DHT22 Humidity and Temperature Sensor
  DS1 = DS18B20 1-Wire Temperature Sensor [part_number=DS18B20]
  S1 = Reed switch [package=THT]
  R1 = Resistor [tolerance=±5% resistance=6.8k package=THT]
  R2 = Resistor [tolerance=±5% resistance=6.8k package=THT]

nets:
  N1: U1.D2, S1.pin_2
  N2: U1.D4, DS1.DQ, R1.Pin_0
  VDD: U1.3V3, DHT1.VDD, DS1.VDD, R1.Pin_1, R2.Pin_0
  GND: U1.GND, DHT1.GND, DS1.GND, S1.pin_1
  N3: U1.D5, DHT1.DATA, R2.Pin_1

custom parts:
  NodeMCU V1.0: ESP9266 based NodeMCU
